# Fritzing sketch buzzer sing (saved by Fritzing 1.0.3b)
breadboards: 1

parts:
  TTP223B2 = TTP223B Capacitive Touch Sensor Module [part_number="Touch sensor"]
  Mod1 = Passive Buzzer
  R1 = Resistor [tolerance=±5% resistance=1k package="0805 [SMD]"]
  U1 = Carte NUCLEO H755ZI-Q
  R2 = Resistor [tolerance=±5% resistance=220 package="0805 [SMD]"]
  R3 = Resistor [tolerance=±5% resistance=150 package="0805 [SMD]"]
  R4 = Resistor [tolerance=±5% resistance=47 package="0805 [SMD]"]
  LED2 = RGB LED (com. cathode, rbg) [color="Red (633nm)" current=0.030A package="5 mm [THT]"]

nets:
  GND: TTP223B2.GND, Mod1.-, R1.Pin_0, U1.GND, LED2.common_cathode
  N1: TTP223B2.VCC, Mod1.S
  N2: TTP223B2.SIG, R1.Pin_1
  N3: R2.Pin_0, LED2.red_anode
  N4: R3.Pin_0, LED2.blue_anode
  N5: R4.Pin_0, LED2.green_anode

custom parts:
  TTP223B Capacitive Touch Sensor Module: The TTP223B capacitive touch sensor module uses the TTP223B IC. The appropriate voltage is approximately 2 to 5.5 volts.
  Carte NUCLEO H755ZI-Q: Carte prototype double coeurs ARM
